// Logisim project Practico 2 nuevo.circ as structural Verilog: 8 circuits, main circuit main
module main (
  input  J,
  input  [7:0] Jaddress,
  output [15:0] Instruccion
);

  wire clock_1_out;
  wire [7:0] contador_1_address;

  Clock clock_1 (.out(clock_1_out));
  Contador contador_1 (.Clock(clock_1_out), .Jump(J), .Jaddr(Jaddress), .Address(contador_1_address));
  ROM #(.dataWidth(16)) rom_1 (.addr(contador_1_address), .data(Instruccion));  // open: sel

  // Notes on the sheet:
  //   contents of rom_1 (hex, n*v repeats v):
  //   123 4567 89ab cdef
endmodule

module Contador (
  input  Clock,
  input  Jump,
  input  [7:0] Jaddr,
  output [7:0] Address
);

  wire and_1_out, and_2_out, and_3_out, and_4_out, and_5_out, and_6_out, demultiplexer_1_out0,
       demultiplexer_1_out1, demultiplexer_2_out0, demultiplexer_2_out1, demultiplexer_3_out0,
       demultiplexer_3_out1, demultiplexer_4_out0, demultiplexer_4_out1, demultiplexer_5_out0,
       demultiplexer_5_out1, demultiplexer_6_out0, demultiplexer_6_out1, demultiplexer_7_out0,
       demultiplexer_7_out1, demultiplexer_8_out0, demultiplexer_8_out1;

  Demultiplexer #(.enable("false")) demultiplexer_1 (
    .out0(demultiplexer_1_out0), .out1(demultiplexer_1_out1), .in(Jump), .sel(Jaddr[0]));
  T_Flip_Flop t_ff_1 (
    .clk(Clock), .T(1'b1), .Q(Address[0]), .preset(demultiplexer_1_out1), .reset(demultiplexer_1_out0));  // open: Qn, en
  Demultiplexer #(.enable("false")) demultiplexer_2 (
    .out0(demultiplexer_2_out0), .out1(demultiplexer_2_out1), .in(Jump), .sel(Jaddr[1]));
  T_Flip_Flop t_ff_2 (
    .clk(Clock), .T(Address[0]), .Q(Address[1]), .preset(demultiplexer_2_out1), .reset(demultiplexer_2_out0));  // open: Qn, en
  and and_1 (and_1_out, Address[1], Address[0]);
  Demultiplexer #(.enable("false")) demultiplexer_3 (
    .out0(demultiplexer_3_out0), .out1(demultiplexer_3_out1), .in(Jump), .sel(Jaddr[2]));
  T_Flip_Flop t_ff_3 (
    .clk(Clock), .T(and_1_out), .Q(Address[2]), .preset(demultiplexer_3_out1), .reset(demultiplexer_3_out0));  // open: Qn, en
  and and_2 (and_2_out, Address[2], and_1_out);
  Demultiplexer #(.enable("false")) demultiplexer_4 (
    .out0(demultiplexer_4_out0), .out1(demultiplexer_4_out1), .in(Jump), .sel(Jaddr[3]));
  T_Flip_Flop t_ff_4 (
    .clk(Clock), .T(and_2_out), .Q(Address[3]), .preset(demultiplexer_4_out1), .reset(demultiplexer_4_out0));  // open: Qn, en
  and and_3 (and_3_out, Address[3], and_2_out);
  Demultiplexer #(.enable("false")) demultiplexer_5 (
    .out0(demultiplexer_5_out0), .out1(demultiplexer_5_out1), .in(Jump), .sel(Jaddr[4]));
  T_Flip_Flop t_ff_5 (
    .clk(Clock), .T(and_3_out), .Q(Address[4]), .preset(demultiplexer_5_out1), .reset(demultiplexer_5_out0));  // open: Qn, en
  and and_4 (and_4_out, Address[4], and_3_out);
  Demultiplexer #(.enable("false")) demultiplexer_6 (
    .out0(demultiplexer_6_out0), .out1(demultiplexer_6_out1), .in(Jump), .sel(Jaddr[5]));
  T_Flip_Flop t_ff_6 (
    .clk(Clock), .T(and_4_out), .Q(Address[5]), .preset(demultiplexer_6_out1), .reset(demultiplexer_6_out0));  // open: Qn, en
  and and_5 (and_5_out, Address[5], and_4_out);
  Demultiplexer #(.enable("false")) demultiplexer_7 (
    .out0(demultiplexer_7_out0), .out1(demultiplexer_7_out1), .in(Jump), .sel(Jaddr[6]));
  T_Flip_Flop t_ff_7 (
    .clk(Clock), .T(and_5_out), .Q(Address[6]), .preset(demultiplexer_7_out1), .reset(demultiplexer_7_out0));  // open: Qn, en
  and and_6 (and_6_out, Address[6], and_5_out);
  Demultiplexer #(.enable("false")) demultiplexer_8 (
    .out0(demultiplexer_8_out0), .out1(demultiplexer_8_out1), .in(Jump), .sel(Jaddr[7]));
  T_Flip_Flop t_ff_8 (
    .clk(Clock), .T(and_6_out), .Q(Address[7]), .preset(demultiplexer_8_out1), .reset(demultiplexer_8_out0));  // open: Qn, en

  // Other names for the same wires on the sheet: Q0 = Address[0]; Q1 = Address[1]; Q2 = Address[2]; Q3 = Address[3];
  //   Q4 = Address[4]; Q5 = Address[5]; Q6 = Address[6]; Q7 = Address[7]; J = Jump; Ja0 = Jaddr[0]; Ja1 = Jaddr[1];
  //   Ja2 = Jaddr[2]; Ja3 = Jaddr[3]; Ja4 = Jaddr[4]; Ja5 = Jaddr[5]; Ja6 = Jaddr[6]; Ja7 = Jaddr[7]
endmodule

module Latch_D_CP (
  input  Habilitador,
  input  Clear,
  input  Dato,
  input  Preset,
  output No_Q,
  output Q
);

  wire and_1_out, and_2_out, nor_1_out, nor_2_out, not_1_out;

  not not_1 (not_1_out, Dato);
  and and_1 (and_1_out, Habilitador, Dato);
  and and_2 (and_2_out, not_1_out, Habilitador);
  nor nor_1 (nor_1_out, and_1_out, Q);
  nor nor_2 (nor_2_out, No_Q, and_2_out);
  or or_1 (No_Q, Clear, nor_1_out);
  or or_2 (Q, nor_2_out, Preset);
endmodule

module Banco_de_registros (
  input  [7:0] IN,
  input  Clk,
  input  Rst,
  input  We,
  input  [3:0] Rd,
  input  [3:0] Rs,
  output [7:0] Out
);

  wire C0, C1, C2, C3, C4, C5, C6, C7, C8, C9, C10, C11, C12, C13, C14, C15, We0, We1, We2, We3, We4, We5,
       We6, We7, We8, We9, WeA, WeB, WeC, WeD, WeE, WeF;
  wire [7:0] Q0, Q1, Q2, Q3, Q4, Q5, Q6, Q7, Q8, Q9, QA, QB, QC, QD, QE, QF;

  Demultiplexer #(.select(4), .enable("false")) demultiplexer_1 (
    .out0(We0), .out1(We1), .out2(We2), .out3(We3), .out4(We4), .out5(We5), .out6(We6), .out7(We7),
    .out8(We8), .out9(We9), .out10(WeA), .out11(WeB), .out12(WeC), .out13(WeD), .out14(WeE), .out15(WeF),
    .in(We), .sel(Rd));
  Demultiplexer #(.select(4), .enable("false")) demultiplexer_2 (
    .out0(C0), .out1(C1), .out2(C2), .out3(C3), .out4(C4), .out5(C5), .out6(C6), .out7(C7), .out8(C8),
    .out9(C9), .out10(C10), .out11(C11), .out12(C12), .out13(C13), .out14(C14), .out15(C15), .in(1'b1),
    .sel(Rs));
  Register register_1 (.D(IN), .en(We0), .Q(Q0), .clk(Clk), .clr(Rst));
  Register register_2 (.D(IN), .en(We2), .Q(Q2), .clk(Clk), .clr(Rst));
  Register register_3 (.D(IN), .en(We4), .Q(Q4), .clk(Clk), .clr(Rst));
  Register register_4 (.D(IN), .en(We6), .Q(Q6), .clk(Clk), .clr(Rst));
  Register register_5 (.D(IN), .en(We8), .Q(Q8), .clk(Clk), .clr(Rst));
  Register register_6 (.D(IN), .en(WeA), .Q(QA), .clk(Clk), .clr(Rst));
  Register register_7 (.D(IN), .en(WeC), .Q(QC), .clk(Clk), .clr(Rst));
  Register register_8 (.D(IN), .en(WeE), .Q(QE), .clk(Clk), .clr(Rst));
  Register register_9 (.D(IN), .en(We1), .Q(Q1), .clk(Clk), .clr(Rst));
  Register register_10 (.D(IN), .en(We3), .Q(Q3), .clk(Clk), .clr(Rst));
  Register register_11 (.D(IN), .en(We5), .Q(Q5), .clk(Clk), .clr(Rst));
  Register register_12 (.D(IN), .en(We7), .Q(Q7), .clk(Clk), .clr(Rst));
  Register register_13 (.D(IN), .en(We9), .Q(Q9), .clk(Clk), .clr(Rst));
  Register register_14 (.D(IN), .en(WeB), .Q(QB), .clk(Clk), .clr(Rst));
  Register register_15 (.D(IN), .en(WeD), .Q(QD), .clk(Clk), .clr(Rst));
  Register register_16 (.D(IN), .en(WeF), .Q(QF), .clk(Clk), .clr(Rst));
  assign Out = C0 ? Q0 : 8'bz;  // Controlled_Buffer controlled_buffer_1
  assign Out = C1 ? Q1 : 8'bz;  // Controlled_Buffer controlled_buffer_2
  assign Out = C2 ? Q2 : 8'bz;  // Controlled_Buffer controlled_buffer_3
  assign Out = C3 ? Q3 : 8'bz;  // Controlled_Buffer controlled_buffer_4
  assign Out = C4 ? Q4 : 8'bz;  // Controlled_Buffer controlled_buffer_5
  assign Out = C5 ? Q5 : 8'bz;  // Controlled_Buffer controlled_buffer_6
  assign Out = C6 ? Q6 : 8'bz;  // Controlled_Buffer controlled_buffer_7
  assign Out = C7 ? Q7 : 8'bz;  // Controlled_Buffer controlled_buffer_8
  assign Out = C8 ? Q8 : 8'bz;  // Controlled_Buffer controlled_buffer_9
  assign Out = C9 ? Q9 : 8'bz;  // Controlled_Buffer controlled_buffer_10
  assign Out = C10 ? QA : 8'bz;  // Controlled_Buffer controlled_buffer_11
  assign Out = C11 ? QB : 8'bz;  // Controlled_Buffer controlled_buffer_12
  assign Out = C12 ? QC : 8'bz;  // Controlled_Buffer controlled_buffer_13
  assign Out = C13 ? QD : 8'bz;  // Controlled_Buffer controlled_buffer_14
  assign Out = C14 ? QE : 8'bz;  // Controlled_Buffer controlled_buffer_15
  assign Out = C15 ? QF : 8'bz;  // Controlled_Buffer controlled_buffer_16
endmodule

module Latch_SR (
  input  S,
  input  H,
  input  R,
  output Q,
  output No_Q
);

  wire nand_1_out, nand_2_out;

  nand nand_1 (nand_1_out, S, H);
  nand nand_2 (nand_2_out, H, R);
  nand nand_3 (Q, nand_1_out, No_Q);
  nand nand_4 (No_Q, Q, nand_2_out);
endmodule

module Latch_D (
  input  D,
  input  H,
  output Q,
  output No_Q
);

  wire nand_1_out, nand_2_out, not_1_out;

  not not_1 (not_1_out, D);
  nand nand_1 (nand_1_out, D, H);
  nand nand_2 (nand_2_out, H, not_1_out);
  nand nand_3 (Q, nand_1_out, No_Q);
  nand nand_4 (No_Q, Q, nand_2_out);
endmodule

module Flip_flop_D (
  input  D,
  input  H,
  output Q,
  output No_Q
);

  wire latch_d_1_q, not_1_out;

  Latch_D latch_d_1 (.D(D), .H(not_1_out), .Q(latch_d_1_q));  // open: No_Q
  not not_1 (not_1_out, H);
  Latch_D latch_d_2 (.D(latch_d_1_q), .H(H), .Q(Q), .No_Q(No_Q));
endmodule

module Registro_PIPO (
  input  [7:0] IN,
  input  We,
  input  Clk,
  output [7:0] OUT
);

  wire and_1_out;

  and and_1 (and_1_out, We, Clk);
  Flip_flop_D flip_flop_d_1 (.D(IN[0]), .H(and_1_out), .Q(OUT[0]));  // open: No_Q
  Flip_flop_D flip_flop_d_2 (.D(IN[1]), .H(and_1_out), .Q(OUT[1]));  // open: No_Q
  Flip_flop_D flip_flop_d_3 (.D(IN[2]), .H(and_1_out), .Q(OUT[2]));  // open: No_Q
  Flip_flop_D flip_flop_d_4 (.D(IN[3]), .H(and_1_out), .Q(OUT[3]));  // open: No_Q
  Flip_flop_D flip_flop_d_5 (.D(IN[5]), .H(and_1_out), .Q(OUT[5]));  // open: No_Q
  Flip_flop_D flip_flop_d_6 (.D(IN[4]), .H(and_1_out), .Q(OUT[4]));  // open: No_Q
  Flip_flop_D flip_flop_d_7 (.D(IN[6]), .H(and_1_out), .Q(OUT[6]));  // open: No_Q
  Flip_flop_D flip_flop_d_8 (.D(IN[7]), .H(and_1_out), .Q(OUT[7]));  // open: No_Q

  // Other names for the same wires on the sheet: I0 = IN[0]; I1 = IN[1]; I2 = IN[2]; I3 = IN[3]; I4 = IN[4];
  //   I5 = IN[5]; I6 = IN[6]; I7 = IN[7]; O0 = OUT[0]; O1 = OUT[1]; O2 = OUT[2]; O3 = OUT[3]; O4 = OUT[4];
  //   O5 = OUT[5]; O6 = OUT[6]; O7 = OUT[7]
endmodule
